# Fritzing sketch ShockCell (saved by Fritzing 0.9.4)

parts:
  U1 = ESP32S-HiLetgo [part_number=ESP32S]
  J3 = Basic Servo
  S1 = Round Pushbutton
  S2 = SWITCH-MOMENTARY-2 [package=reed_switch_plastic]

nets:
  N1: U1.EN, J3.pulse
  N2: U1.GPIO39, S2.1
  N3: U1.GND, S1.leg1, S2.2
  N4: U1.GPIO13, S1.leg0

notes:
  Wi-Fi
  - SSID
  - WLAN Passwort
  Telegram bot
  Chastikey
  IFTTT

custom parts:
  ESP32S-HiLetgo: HiLetgo ESP-WROOM-32 ESP32 ESP-32S Development Board 2.4GHz Dual-Mode WiFi + Bluetooth Dual Cores Microcontroller The ESP32 integrated with Antenna switches, RF Balun, power amplifiers, low-noise amplifiers, filters, and management modules, and the entire solution occupies the least area of PCB. 2.4 GHz Wi-Fi plus Bluetooth dual-mode chip, with TSMC Ultra-low power consumption 40nm technology,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
